# Fritzing sketch Sketch (saved by Fritzing 0.9.3b)
breadboards: 2

parts:
  元件1 = Arduino Uno (Rev3)
  Disp1 = LBT2088AH [part_number=LBT2088AH]

nets:
  N1: 元件1.A0, Disp1.pin_6
  N2: 元件1.A1, Disp1.pin_11
  N3: 元件1.A2, Disp1.pin_15
  N4: 元件1.A3, Disp1.pin_16
  N5: 元件1.D8, Disp1.pin_14
  N6: 元件1.D9_PWM, Disp1.pin_9
  N7: 元件1.D10_PWM/SS, Disp1.pin_13
  N8: 元件1.D11_PWM/MOSI, Disp1.pin_3
  N9: 元件1.D12/MISO, Disp1.pin_4
  N10: 元件1.D13/SCK, Disp1.pin_10
  N11: 元件1.D2, Disp1.pin_5
  N12: 元件1.D3_PWM, Disp1.pin2
  N13: 元件1.D4, Disp1.pin_7
  N14: 元件1.D5_PWM, Disp1.pin1
  N15: 元件1.D6_PWM, Disp1.pin_12
  N16: 元件1.D7, Disp1.pin_8

// code stored in the sketch: main.ino
const int line[] PROGMEM={2,3,4,5,6,7,8,9};
const int column[] PROGMEM={10,11,12,13,A0,A1,A2,A3};
const int frame[8][40] PROGMEM={
    {0,0,0,0,0,0,0,0,0,1,0,0,0,0,0,0,0,0,0,0,0,0,0,0,0,0,0,0,0,0,0,0,0,0,0,0,0,0,0,0},
    {0,0,1,0,1,1,0,0,0,0,0,0,0,0,0,0,0,0,0,0,0,0,0,0,0,0,1,1,1,1,0,0,0,0,0,0,0,0,0,0},
    {0,0,1,1,0,0,1,0,1,1,0,0,0,0,1,1,1,0,0,0,1,1,1,0,0,1,0,0,0,0,1,0,0,0,0,0,0,0,0,0},
    {0,0,1,0,0,0,1,0,0,1,0,0,0,1,0,0,0,1,0,1,0,0,0,1,0,0,1,1,1,1,1,0,0,0,0,0,0,0,0,0},
    {0,0,1,0,0,0,1,0,0,1,0,0,0,1,0,0,0,1,0,1,0,0,0,1,0,1,0,0,0,0,1,0,0,0,0,0,0,0,0,0},
    {0,0,1,0,0,0,1,0,0,1,0,0,0,0,1,1,1,1,0,0,1,1,1,1,0,1,0,0,0,0,1,0,0,0,0,0,0,0,0,0},
    {0,0,1,0,0,0,1,0,1,1,1,0,0,0,0,0,0,1,0,0,0,0,0,1,0,0,1,1,1,1,0,1,1,0,0,0,0,0,0,0},
    {0,0,0,0,0,0,0,0,0,0,0,0,0,1,1,1,1,0,0,1,1,1,1,0,0,0,0,0,0,0,0,0,0,0,0,0,0,0,0,0}
};
double pos=0.01;
/*const int frame[8][40]={
    {0,0,0,0,0,0,0,0,0,0,0,0,0,0,0,0,0,0,0,0,0,0,0,0,0,0,0,0,0,0,0,0,0,0,0,0,0,0,0,0},
    {0,0,0,0,0,0,0,0,0,0,0,0,0,0,0,0,0,0,0,0,0,0,0,0,0,0,0,0,0,0,0,0,0,0,0,0,0,0,0,0},
    {0,0,0,0,0,0,0,0,0,0,0,0,0,0,0,0,0,0,0,0,0,0,0,0,0,0,0,0,0,0,0,0,0,0,0,0,0,0,0,0},
    {0,0,0,0,0,0,0,0,0,0,0,0,0,0,0,0,0,0,0,0,0,0,0,0,0,0,0,0,0,0,0,0,0,0,0,0,0,0,0,0},
    {0,0,0,0,0,0,0,0,0,0,0,0,0,0,0,0,0,0,0,0,0,0,0,0,0,0,0,0,0,0,0,0,0,0,0,0,0,0,0,0},
    {0,0,0,0,0,0,0,0,0,0,0,0,0,0,0,0,0,0,0,0,0,0,0,0,0,0,0,0,0,0,0,0,0,0,0,0,0,0,0,0},
    {0,0,0,0,0,0,0,0,0,0,0,0,0,0,0,0,0,0,0,0,0,0,0,0,0,0,0,0,0,0,0,0,0,0,0,0,0,0,0,0},
    {0,0,0,0,0,0,0,0,0,0,0,0,0,0,0,0,0,0,0,0,0,0,0,0,0,0,0,0,0,0,0,0,0,0,0,0,0,0,0,0}
}*/
void setup() {
	for(int i=0;i<8;i++){
        pinMode(line[i],OUTPUT);
        pinMode(column[i],OUTPUT);
        digitalWrite(line[i],LOW);
        digitalWrite(column[i],HIGH);
    }
}

void loop() {
    for(int l=0;l<8;l++){
        for(int c=0;c<8;c++){
            if(frame[c][l+(int)(floor(pos))]==1){
                digitalWrite(line[l],HIGH);
                digitalWrite(column[c],LOW);
                delay(1);
                digitalWrite(line[l],LOW);
                digitalWrite(column[c],HIGH);
                pos+=0.02;
            }
        }
    }
    if(pos>=40.0){
        pos=0.01;
    }
}


/*int supersonic_func1(){
    digitalWrite(trig,LOW);
    delayMicroseconds(2);
    digitalWrite(trig,HIGH);
    delayMicroseconds(10);
    digitalWrite(trig,LOW);
    /*
    v=340 m/s
    t=s/v
    s=t*0.034/2
    */
    /*duration=pulseIn(echo,HIGH);
    distance= duration*0.034/2;
    Serial.println(distance);
}*/
